# Fritzing sketch turnout_decoder_nano (saved by Fritzing 0.9.3b)
circuit board: 8.5cm x 10cm
breadboards: 1

parts:
  J9 = double row female pin header, 20 pins [form="♀ (female)"]
  MCP23017 = female pin header, 10 pins [form="♀ (female)"]
  J11 = male pin header, 4 pins [form="♂ (male)"]
  J15 = male pin header, 4 pins [form="♂ (male)"]
  Nano = Arduino Nano (Rev3.0)
  J18 = Screw terminal - 2 pins [package=THT]
  -2 = female pin header, 2 pins [form="♀ (female)"]
  BR3 = female alternating pin header, 2 pins [form="♀ (female)"]
  C2 = Electrolytic Capacitor [capacitance=22µF voltage=20V package="100 mil [THT, electrolytic]"]
  C1 = Tantalum Capacitor [capacitance=1µF voltage=20V package="100 mil [THT, tantalum]"]
  C3 = Tantalum Capacitor [capacitance=1µF voltage=20V package="100 mil [THT, tantalum]"]
  IC2 = IC, DIP package, 8 pins [chip_label=IC]
  R1 = Resistor [tolerance=±5% resistance=1k power=0.25 package=THT]
  D1 = Rectifier Diode [part_number=1N4001 package="300 mil [THT]"]
  C4 = Ceramic Capacitor [capacitance=100nF package="100 mil [THT, multilayer]"]
  R2 = Resistor [tolerance=±5% resistance=10k power=0.25 package=THT]
  R3 = Resistor [tolerance=±5% resistance=10k power=0.25 package=THT]
  U1 = Voltage Regulator - 5V [package="TO220 [THT]"]
  J19 = female pin header, 8 pins [form="♀ (female)"]
  J20 = female pin header, 8 pins [form="♀ (female)"]
  J21 = female pin header, 12 pins [form="♀ (female)"]
  J22 = female pin header, 2 pins [form="♀ (female)"]

nets:
  N1: J9.pin1, J20.pin8
  N2: J9.pin2, J20.pin7
  N3: J9.pin3, J20.pin6
  N4: J9.pin4, J20.pin5
  N5: J9.pin5, J20.pin4
  N6: J9.pin6, J20.pin3
  N7: J9.pin7, J20.pin2
  N8: J9.pin8, J20.pin1
  N9: J9.pin13, J19.pin1
  N10: J9.pin14, J19.pin2
  N11: J9.pin15, J19.pin3
  N12: J9.pin16, J19.pin4
  N13: J9.pin17, J19.pin5
  N14: J9.pin18, J19.pin6
  N15: J9.pin19, J19.pin7
  N16: J9.pin20, J19.pin8
  N17: MCP23017.pin1, J11.pin1, J15.pin1, Nano.5V, C2.+, C3.+, IC2.pin8, R2.Pin_1, R3.Pin_1, U1.output_voltage, J22.pin2
  GND: MCP23017.pin2, MCP23017.pin8, MCP23017.pin9, MCP23017.pin10, J11.pin2, J15.pin2, Nano.GND, -2.pin1, C2.-, C1.-, C3.-, IC2.pin5, U1.GND, J21.pin12, J22.pin1
  N18: MCP23017.pin3, J11.pin4, J15.pin4, Nano.A5
  N19: MCP23017.pin4, J11.pin3, J15.pin3, Nano.A4
  N20: Nano.D2, IC2.pin6, R2.Pin_0
  N21: Nano.D3, J21.pin11
  N22: Nano.D4, J21.pin10
  N23: Nano.D5, J21.pin9
  N24: Nano.D6, J21.pin8
  N25: Nano.D7, J21.pin7
  N26: Nano.D8, J21.pin6
  N27: Nano.D9, J21.pin5
  N28: Nano.D10, J21.pin4
  N29: Nano.D11/MOSI, J21.pin3
  N30: Nano.D12/MISO, J21.pin2
  N31: Nano.D13/SCK, J21.pin1
  N32: J18.pin1, BR3.pin1, R1.Pin_0
  N33: J18.pin2, -2.pin2, IC2.pin3, D1.anode, C4.1
  N34: BR3.pin2, C1.+, U1.input_voltage
  N35: IC2.pin2, R1.Pin_1, D1.cathode, C4.0
  N36: IC2.pin7, R3.Pin_0

notes:
  VCC
  GND
  SCL
  SDA
  A0
  A1
  A2
  A3
  A4
  A5
  A6
  A7
  B0
  B1
  B2
  B3
  B4
  B6
  B5
  B7
  1
  4x4DCCTD4
  +
  DCC In
  D13
  D12
  D11
  D10
  D09
  D08
  D07
  D06
  D05
  D04
  D03
  0
  2
  3
  4
  5
  6
  7
  9
  10
  11
  12
  13
  14
  15
  8
  +5V
